# Fritzing sketch motor driver (saved by Fritzing 0.9.10b)
breadboards: 1

parts:
  Composant1 = Arduino Nano (Rev3.0)
  C1 = Electrolytic Capacitor [capacitance=1µF voltage=35V package="100 mil [THT, electrolytic]"]
  J1_12_V = Power Jack [package=power_jack_combo]
  R1 = Rotary Potentiometer (Small) [maximum_resistance=100kΩ knob_status=50% power=0.5W package=THT]
  U1 = SWITCH_SPDT [package=kps-1290]
  R2 = Resistor [tolerance=±5% resistance=10k package="0402 [SMD]"]
  L298N1 = L298N DC motor driver
  M1 = DC Motor [voltage_(max)=6V voltage_(min)=3V]

nets:
  GND: Composant1.GND, C1.-, J1_12_V.GND, R1.leg2, U1.S, L298N1.GND
  N1: Composant1.D5, L298N1.IN2
  N2: Composant1.D6, L298N1.IN1
  VIN: Composant1.VIN, C1.+, J1_12_V.PWR, L298N1.12V
  N3: Composant1.5V, R1.leg1, U1.O, R2.Pin_0, L298N1.5V#7
  N4: Composant1.A3, R1.wiper
  N5: Composant1.A1, U1.P, R2.Pin_1
  N6: L298N1.OUT1, M1.pin_2
  N7: L298N1.OUT2, M1.pin_1
  N8: L298N1.5V#9, L298N1.ENA

custom parts:
  L298N DC motor driver: 2x DC motor driver with 78M05 positive voltage regulator (7..35 V) L298N: max 46 V, 2 A Set 5 V Enable jumper to enable 5 V regultor (needed for the L298N) and +5 V output at screw terminal or supply external +5 V at screw terminal Set ENA and/or ENB to +5 V to enable motor permanently or supply ENA and/or ENB with PWM signal IN1 and IN2 set rotation directory for motor A (OUT1/OUT2) IN2 and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
